# Fritzing sketch smartwatch-layout (saved by Fritzing 0.9.1b)
breadboards: 1

parts:
  RF1 = nRF8001 Bluetooth LE Breakout
  Part1 = Arduino Uno (Rev3)
  OLED1 = 128x64 Monochrom OLED Display with SPI Control
  R1 = Resistor [tolerance=±5% resistance=1M package="1206 [SMD]"]
  J1 = Piezo Speaker

nets:
  N1: RF1.SCK, Part1.D13/SCK
  N2: RF1.MISO, Part1.D12/MISO
  N3: RF1.MOSI, Part1.D11_PWM/MOSI
  N4: RF1.REQ, Part1.D10_PWM/SS
  N5: RF1.RDY, Part1.D2
  N6: RF1.RST, Part1.D9_PWM
  GND: RF1.GND, Part1.GND, OLED1.GND, R1.Pin_0, J1.pin1
  VIN: RF1.VIN, Part1.5V, OLED1.Vin
  N7: Part1.A0, R1.Pin_1, J1.pin2
  N8: Part1.D8, OLED1.Reset
  N9: Part1.D4, OLED1.Clock
  N10: Part1.D5_PWM, OLED1.Data
  N11: Part1.D6_PWM, OLED1.CS
  N12: Part1.D7, OLED1.SA0/DC

notes:
  Bluetooth
  SCK - 13
  MISO - 12
  MOSI - 11
  REQ - 10
  RST - 9
  RDY - 2
  OLED
  DC - 7
  CS - 6
  CLK - 4
  DATA - 5
  RESET - 8

custom parts:
  nRF8001 Bluetooth LE Breakout: nRF8001 Breakout Board
